# Fritzing sketch sketch (saved by Fritzing 0.8.5b)
breadboards: 1

parts:
  TRINKET1 = Trinket 5V
  INA1 = INA219 DC Current Sensor Breakout

nets:
  N1: TRINKET1.no_name_yet#2, INA1.GND
  N2: TRINKET1.no_name_yet#6, INA1.VCC
  N3: TRINKET1.no_name_yet#7, INA1.SCL
  N4: TRINKET1.no_name_yet#9, INA1.SDA

notes:
  load
  power

custom parts:
  Trinket 5V: Adafruit Trinket 5V
  INA219 DC Current Sensor Breakout: INA DC Current Sensor Breakout
